# Fritzing sketch 74hc595_expandidido (saved by Fritzing 0.9.4)
circuit board: 20cm x 15cm
breadboards: 1

parts:
  74HC595 = 74HC595 [package="DIP16 [THT]"]
  Q1 = NPN-Transistor [package="TO92 [THT]"]
  LED1 = LED - 5mm [color="Red (633nm)" package="5 mm [THT]"]
  LED2 = LED - 5mm [color="Red (633nm)" package="5 mm [THT]"]
  LED4 = LED - 5mm [color="Red (633nm)" package="5 mm [THT]"]
  LED5 = LED - 5mm [color="Red (633nm)" package="5 mm [THT]"]
  LED6 = LED - 5mm [color="Red (633nm)" package="5 mm [THT]"]
  LED8 = LED - 5mm [color="Red (633nm)" package="5 mm [THT]"]
  LED7 = LED - 5mm [color="Red (633nm)" package="5 mm [THT]"]
  R1 = Resistor [tolerance=±5% resistance=220 package=THT]
  R2 = Resistor [tolerance=±5% resistance=220 package=THT]
  R3 = Resistor [tolerance=±5% resistance=220 package=THT]
  R4 = Resistor [tolerance=±5% resistance=220 package=THT]
  R5 = Resistor [tolerance=±5% resistance=220 package=THT]
  R6 = Resistor [tolerance=±5% resistance=220 package=THT]
  R7 = Resistor [tolerance=±5% resistance=220 package=THT]
  R8 = Resistor [tolerance=±5% resistance=220 package=THT]
  R9 = Resistor [tolerance=±5% resistance=4.7k package=THT]
  R10 = Resistor [tolerance=±5% resistance=4.7k package=THT]
  R11 = Resistor [tolerance=±5% resistance=4.7k package=THT]
  R12 = Resistor [tolerance=±5% resistance=4.7k package=THT]
  R13 = Resistor [tolerance=±5% resistance=4.7k package=THT]
  R14 = Resistor [tolerance=±5% resistance=4.7k package=THT]
  R15 = Resistor [tolerance=±5% resistance=4.7k package=THT]
  R16 = Resistor [tolerance=±5% resistance=4.7k package=THT]
  In_12V = male pin header, 2 pins [form="♂ (male)"]
  74HC165 = 74HC595 [package="DIP16 [THT]"]
  R17 = Resistor [tolerance=±5% resistance=10k package=THT]
  R18 = Resistor [tolerance=±5% resistance=10k package=THT]
  R19 = Resistor [tolerance=±5% resistance=10k package=THT]
  R20 = Resistor [tolerance=±5% resistance=10k package=THT]
  R21 = Resistor [tolerance=±5% resistance=10k package=THT]
  R22 = Resistor [tolerance=±5% resistance=10k package=THT]
  R23 = Resistor [tolerance=±5% resistance=10k package=THT]
  R24 = Resistor [tolerance=±5% resistance=10k package=THT]
  C1 = Electrolytic Capacitor [capacitance=0.1mF package="100 mil [THT, electrolytic]"]
  S1 = Pushbutton [package="[THT]"]
  S2 = Pushbutton [package="[THT]"]
  S3 = Pushbutton [package="[THT]"]
  S4 = Pushbutton [package="[THT]"]
  S5 = Pushbutton [package="[THT]"]
  S6 = Pushbutton [package="[THT]"]
  S7 = Pushbutton [package="[THT]"]
  S8 = Pushbutton [package="[THT]"]
  LED3 = LED - 5mm [color="Red (633nm)" package="5 mm [THT]"]
  Q9 = NPN-Transistor [package="TO92 [THT]"]
  Q10 = NPN-Transistor [package="TO92 [THT]"]
  Q11 = NPN-Transistor [package="TO92 [THT]"]
  Q12 = NPN-Transistor [package="TO92 [THT]"]
  Q13 = NPN-Transistor [package="TO92 [THT]"]
  Q14 = NPN-Transistor [package="TO92 [THT]"]
  Q15 = NPN-Transistor [package="TO92 [THT]"]
  Out_12V = male pin header, 2 pins [form="♂ (male)"]
  D_165 = male pin header, 3 pins [form="♂ (male)"]
  O/7 = female pin header, 2 pins [form="♀ (female)"]
  O/5 = female pin header, 2 pins [form="♀ (female)"]
  O/6 = female pin header, 2 pins [form="♀ (female)"]
  O/4 = female pin header, 2 pins [form="♀ (female)"]
  O/3 = female pin header, 2 pins [form="♀ (female)"]
  O/2 = female pin header, 2 pins [form="♀ (female)"]
  O/1 = female pin header, 2 pins [form="♀ (female)"]
  O/0 = female pin header, 2 pins [form="♀ (female)"]
  out_5V = male pin header, 2 pins [form="♂ (male)"]
  in_5V = male pin header, 2 pins [form="♂ (male)"]
  in_shif = male pin header, 3 pins [form="♂ (male)"]
  out_shift = male pin header, 3 pins [form="♂ (male)"]
  Leds = male pin header, 2 pins [form="♂ (male)"]
  D_165_2 = female pin header, 3 pins [form="♀ (female)"]
  O_165 = female pin header, 3 pins [form="♀ (female)"]
  D_166 = male pin header, 3 pins [form="♂ (male)"]
  R25 = Resistor [tolerance=±5% resistance=10k package=THT]
  R26 = Resistor [tolerance=±5% resistance=10k package=THT]
  R27 = Resistor [tolerance=±5% resistance=10k package=THT]
  R28 = Resistor [tolerance=±5% resistance=10k package=THT]
  R29 = Resistor [tolerance=±5% resistance=10k package=THT]
  R30 = Resistor [tolerance=±5% resistance=10k package=THT]
  R31 = Resistor [tolerance=±5% resistance=10k package=THT]
  R32 = Resistor [tolerance=±5% resistance=10k package=THT]
  C2 = Electrolytic Capacitor [capacitance=0.1mF package="100 mil [THT, electrolytic]"]
  S9 = Pushbutton [package="[THT]"]
  S10 = Pushbutton [package="[THT]"]
  S11 = Pushbutton [package="[THT]"]
  S12 = Pushbutton [package="[THT]"]
  S13 = Pushbutton [package="[THT]"]
  S14 = Pushbutton [package="[THT]"]
  S15 = Pushbutton [package="[THT]"]
  S16 = Pushbutton [package="[THT]"]
  74HC596 = 74HC595 [package="DIP16 [THT]"]
  74HC597 = 74HC595 [package="DIP16 [THT]"]
  Q16 = NPN-Transistor [package="TO92 [THT]"]
  Q17 = NPN-Transistor [package="TO92 [THT]"]
  Q18 = NPN-Transistor [package="TO92 [THT]"]
  Q19 = NPN-Transistor [package="TO92 [THT]"]
  Q20 = NPN-Transistor [package="TO92 [THT]"]
  Q21 = NPN-Transistor [package="TO92 [THT]"]
  Q22 = NPN-Transistor [package="TO92 [THT]"]
  Q23 = NPN-Transistor [package="TO92 [THT]"]
  Leds1 = male pin header, 2 pins [form="♂ (male)"]
  O/8 = female pin header, 2 pins [form="♀ (female)"]
  O/9 = female pin header, 2 pins [form="♀ (female)"]
  O/10 = female pin header, 2 pins [form="♀ (female)"]
  O/11 = female pin header, 2 pins [form="♀ (female)"]
  O/12 = female pin header, 2 pins [form="♀ (female)"]
  O/13 = female pin header, 2 pins [form="♀ (female)"]
  O/14 = female pin header, 2 pins [form="♀ (female)"]
  O/15 = female pin header, 2 pins [form="♀ (female)"]
  out_shift1 = male pin header, 3 pins [form="♂ (male)"]
  O_166 = female pin header, 3 pins [form="♀ (female)"]
  D_167 = female pin header, 3 pins [form="♀ (female)"]
  in_shif1 = male pin header, 3 pins [form="♂ (male)"]
  out_5V1 = male pin header, 2 pins [form="♂ (male)"]
  Out_12V1 = male pin header, 2 pins [form="♂ (male)"]
  In_12V1 = male pin header, 2 pins [form="♂ (male)"]
  in_5V1 = male pin header, 2 pins [form="♂ (male)"]
  LED9 = LED - 5mm [color="Red (633nm)" package="5 mm [THT]"]
  LED10 = LED - 5mm [color="Red (633nm)" package="5 mm [THT]"]
  LED11 = LED - 5mm [color="Red (633nm)" package="5 mm [THT]"]
  LED12 = LED - 5mm [color="Red (633nm)" package="5 mm [THT]"]
  LED13 = LED - 5mm [color="Red (633nm)" package="5 mm [THT]"]
  LED14 = LED - 5mm [color="Red (633nm)" package="5 mm [THT]"]
  LED15 = LED - 5mm [color="Red (633nm)" package="5 mm [THT]"]
  LED16 = LED - 5mm [color="Red (633nm)" package="5 mm [THT]"]
  R33 = Resistor [tolerance=±5% resistance=220 package=THT]
  R34 = Resistor [tolerance=±5% resistance=220 package=THT]
  R35 = Resistor [tolerance=±5% resistance=220 package=THT]
  R36 = Resistor [tolerance=±5% resistance=220 package=THT]
  R37 = Resistor [tolerance=±5% resistance=220 package=THT]
  R38 = Resistor [tolerance=±5% resistance=220 package=THT]
  R39 = Resistor [tolerance=±5% resistance=220 package=THT]
  R40 = Resistor [tolerance=±5% resistance=220 package=THT]
  R41 = Resistor [tolerance=±5% resistance=4.7k package=THT]
  R42 = Resistor [tolerance=±5% resistance=4.7k package=THT]
  R43 = Resistor [tolerance=±5% resistance=4.7k package=THT]
  R44 = Resistor [tolerance=±5% resistance=4.7k package=THT]
  R45 = Resistor [tolerance=±5% resistance=4.7k package=THT]
  R46 = Resistor [tolerance=±5% resistance=4.7k package=THT]
  R47 = Resistor [tolerance=±5% resistance=4.7k package=THT]
  R48 = Resistor [tolerance=±5% resistance=4.7k package=THT]
  D_168 = male pin header, 3 pins [form="♂ (male)"]
  D_169 = male pin header, 3 pins [form="♂ (male)"]
  R49 = Resistor [tolerance=±5% resistance=10k package=THT]
  R50 = Resistor [tolerance=±5% resistance=10k package=THT]
  R51 = Resistor [tolerance=±5% resistance=10k package=THT]
  R52 = Resistor [tolerance=±5% resistance=10k package=THT]
  R53 = Resistor [tolerance=±5% resistance=10k package=THT]
  R54 = Resistor [tolerance=±5% resistance=10k package=THT]
  R55 = Resistor [tolerance=±5% resistance=10k package=THT]
  R56 = Resistor [tolerance=±5% resistance=10k package=THT]
  R57 = Resistor [tolerance=±5% resistance=10k package=THT]
  R58 = Resistor [tolerance=±5% resistance=10k package=THT]
  R59 = Resistor [tolerance=±5% resistance=10k package=THT]
  R60 = Resistor [tolerance=±5% resistance=10k package=THT]
  R61 = Resistor [tolerance=±5% resistance=10k package=THT]
  R62 = Resistor [tolerance=±5% resistance=10k package=THT]
  R63 = Resistor [tolerance=±5% resistance=10k package=THT]
  R64 = Resistor [tolerance=±5% resistance=10k package=THT]
  C3 = Electrolytic Capacitor [capacitance=0.1mF package="100 mil [THT, electrolytic]"]
  C4 = Electrolytic Capacitor [capacitance=0.1mF package="100 mil [THT, electrolytic]"]
  S17 = Pushbutton [package="[THT]"]
  S18 = Pushbutton [package="[THT]"]
  S19 = Pushbutton [package="[THT]"]
  S20 = Pushbutton [package="[THT]"]
  S21 = Pushbutton [package="[THT]"]
  S22 = Pushbutton [package="[THT]"]
  S23 = Pushbutton [package="[THT]"]
  S24 = Pushbutton [package="[THT]"]
  S25 = Pushbutton [package="[THT]"]
  S26 = Pushbutton [package="[THT]"]
  S27 = Pushbutton [package="[THT]"]
  S28 = Pushbutton [package="[THT]"]
  S29 = Pushbutton [package="[THT]"]
  S30 = Pushbutton [package="[THT]"]
  S31 = Pushbutton [package="[THT]"]
  S32 = Pushbutton [package="[THT]"]
  74HC598 = 74HC595 [package="DIP16 [THT]"]
  74HC599 = 74HC595 [package="DIP16 [THT]"]
  74HC600 = 74HC595 [package="DIP16 [THT]"]
  74HC601 = 74HC595 [package="DIP16 [THT]"]
  Q24 = NPN-Transistor [package="TO92 [THT]"]
  Q25 = NPN-Transistor [package="TO92 [THT]"]
  Q26 = NPN-Transistor [package="TO92 [THT]"]
  Q27 = NPN-Transistor [package="TO92 [THT]"]
  Q28 = NPN-Transistor [package="TO92 [THT]"]
  Q29 = NPN-Transistor [package="TO92 [THT]"]
  Q30 = NPN-Transistor [package="TO92 [THT]"]
  Q31 = NPN-Transistor [package="TO92 [THT]"]
  Q32 = NPN-Transistor [package="TO92 [THT]"]
  Q33 = NPN-Transistor [package="TO92 [THT]"]
  Q34 = NPN-Transistor [package="TO92 [THT]"]
  Q35 = NPN-Transistor [package="TO92 [THT]"]
  Q36 = NPN-Transistor [package="TO92 [THT]"]
  Q37 = NPN-Transistor [package="TO92 [THT]"]
  Q38 = NPN-Transistor [package="TO92 [THT]"]
  Q39 = NPN-Transistor [package="TO92 [THT]"]
  Leds2 = male pin header, 2 pins [form="♂ (male)"]
  Leds3 = male pin header, 2 pins [form="♂ (male)"]
  O/16 = female pin header, 2 pins [form="♀ (female)"]
  O/17 = female pin header, 2 pins [form="♀ (female)"]
  O/18 = female pin header, 2 pins [form="♀ (female)"]
  O/19 = female pin header, 2 pins [form="♀ (female)"]
  O/20 = female pin header, 2 pins [form="♀ (female)"]
  O/21 = female pin header, 2 pins [form="♀ (female)"]
  O/22 = female pin header, 2 pins [form="♀ (female)"]
  O/23 = female pin header, 2 pins [form="♀ (female)"]
  O/24 = female pin header, 2 pins [form="♀ (female)"]
  O/25 = female pin header, 2 pins [form="♀ (female)"]
  O/26 = female pin header, 2 pins [form="♀ (female)"]
  O/27 = female pin header, 2 pins [form="♀ (female)"]
  O/28 = female pin header, 2 pins [form="♀ (female)"]
  O/29 = female pin header, 2 pins [form="♀ (female)"]
  O/30 = female pin header, 2 pins [form="♀ (female)"]
  O/31 = female pin header, 2 pins [form="♀ (female)"]
  out_shift2 = male pin header, 3 pins [form="♂ (male)"]
  out_shift3 = male pin header, 3 pins [form="♂ (male)"]
  O_167 = female pin header, 3 pins [form="♀ (female)"]
  O_168 = female pin header, 3 pins [form="♀ (female)"]
  D_170 = female pin header, 3 pins [form="♀ (female)"]
  D_171 = female pin header, 3 pins [form="♀ (female)"]
  in_shif2 = male pin header, 3 pins [form="♂ (male)"]
  in_shif3 = male pin header, 3 pins [form="♂ (male)"]
  out_5V2 = male pin header, 2 pins [form="♂ (male)"]
  out_5V3 = male pin header, 2 pins [form="♂ (male)"]
  Out_12V2 = male pin header, 2 pins [form="♂ (male)"]
  Out_12V3 = male pin header, 2 pins [form="♂ (male)"]
  In_12V2 = male pin header, 2 pins [form="♂ (male)"]
  In_12V3 = male pin header, 2 pins [form="♂ (male)"]
  in_5V2 = male pin header, 2 pins [form="♂ (male)"]
  in_5V3 = male pin header, 2 pins [form="♂ (male)"]
  LED17 = LED - 5mm [color="Red (633nm)" package="5 mm [THT]"]
  LED18 = LED - 5mm [color="Red (633nm)" package="5 mm [THT]"]
  LED19 = LED - 5mm [color="Red (633nm)" package="5 mm [THT]"]
  LED20 = LED - 5mm [color="Red (633nm)" package="5 mm [THT]"]
  LED21 = LED - 5mm [color="Red (633nm)" package="5 mm [THT]"]
  LED22 = LED - 5mm [color="Red (633nm)" package="5 mm [THT]"]
  LED23 = LED - 5mm [color="Red (633nm)" package="5 mm [THT]"]
  LED24 = LED - 5mm [color="Red (633nm)" package="5 mm [THT]"]
  LED25 = LED - 5mm [color="Red (633nm)" package="5 mm [THT]"]
  LED26 = LED - 5mm [color="Red (633nm)" package="5 mm [THT]"]
  LED27 = LED - 5mm [color="Red (633nm)" package="5 mm [THT]"]
  LED28 = LED - 5mm [color="Red (633nm)" package="5 mm [THT]"]
  LED29 = LED - 5mm [color="Red (633nm)" package="5 mm [THT]"]
  LED30 = LED - 5mm [color="Red (633nm)" package="5 mm [THT]"]
  LED31 = LED - 5mm [color="Red (633nm)" package="5 mm [THT]"]
  LED32 = LED - 5mm [color="Red (633nm)" package="5 mm [THT]"]
  R65 = Resistor [tolerance=±5% resistance=220 package=THT]
  R66 = Resistor [tolerance=±5% resistance=220 package=THT]
  R67 = Resistor [tolerance=±5% resistance=220 package=THT]
  R68 = Resistor [tolerance=±5% resistance=220 package=THT]
  R69 = Resistor [tolerance=±5% resistance=220 package=THT]
  R70 = Resistor [tolerance=±5% resistance=220 package=THT]
  R71 = Resistor [tolerance=±5% resistance=220 package=THT]
  R72 = Resistor [tolerance=±5% resistance=220 package=THT]
  R73 = Resistor [tolerance=±5% resistance=220 package=THT]
  R74 = Resistor [tolerance=±5% resistance=220 package=THT]
  R75 = Resistor [tolerance=±5% resistance=220 package=THT]
  R76 = Resistor [tolerance=±5% resistance=220 package=THT]
  R77 = Resistor [tolerance=±5% resistance=220 package=THT]
  R78 = Resistor [tolerance=±5% resistance=220 package=THT]
  R79 = Resistor [tolerance=±5% resistance=220 package=THT]
  R80 = Resistor [tolerance=±5% resistance=220 package=THT]
  R81 = Resistor [tolerance=±5% resistance=4.7k package=THT]
  R82 = Resistor [tolerance=±5% resistance=4.7k package=THT]
  R83 = Resistor [tolerance=±5% resistance=4.7k package=THT]
  R84 = Resistor [tolerance=±5% resistance=4.7k package=THT]
  R85 = Resistor [tolerance=±5% resistance=4.7k package=THT]
  R86 = Resistor [tolerance=±5% resistance=4.7k package=THT]
  R87 = Resistor [tolerance=±5% resistance=4.7k package=THT]
  R88 = Resistor [tolerance=±5% resistance=4.7k package=THT]
  R89 = Resistor [tolerance=±5% resistance=4.7k package=THT]
  R90 = Resistor [tolerance=±5% resistance=4.7k package=THT]
  R91 = Resistor [tolerance=±5% resistance=4.7k package=THT]
  R92 = Resistor [tolerance=±5% resistance=4.7k package=THT]
  R93 = Resistor [tolerance=±5% resistance=4.7k package=THT]
  R94 = Resistor [tolerance=±5% resistance=4.7k package=THT]
  R95 = Resistor [tolerance=±5% resistance=4.7k package=THT]
  R96 = Resistor [tolerance=±5% resistance=4.7k package=THT]
  entradas_sinal = male pin header, 9 pins [form="♂ (male)"]
  entradas_sinal1 = male pin header, 9 pins [form="♂ (male)"]
  entradas_sinal2 = male pin header, 9 pins [form="♂ (male)"]
  entradas_sinal3 = male pin header, 9 pins [form="♂ (male)"]

nets:
  N1: 74HC595.Q1, LED2.anode, R10.Pin_1
  N2: 74HC595.Q2, R11.Pin_1, LED3.anode
  N3: 74HC595.Q3, LED4.anode, R12.Pin_1
  N4: 74HC595.Q4, LED5.anode, R13.Pin_1
  N5: 74HC595.Q5, LED6.anode, R14.Pin_1
  N6: 74HC595.Q6, LED7.anode, R15.Pin_1
  N7: 74HC595.Q7, LED8.anode, R16.Pin_1
  GND: 74HC595.GND, 74HC595.OE, In_12V.pin2, 74HC165.GND, R17.Pin_1, R18.Pin_1, R19.Pin_1, R20.Pin_1, R21.Pin_1, R22.Pin_1, R23.Pin_1, R24.Pin_1, C1.-, Out_12V.pin2, O/7.pin2, O/5.pin2, O/6.pin2, O/4.pin2, O/3.pin2, O/2.pin2, O/1.pin2, O/0.pin2, out_5V.pin2, in_5V.pin2, Leds.pin2
  N8: 74HC595.Q7', out_shift.pin1
  5V: 74HC595.MR, 74HC595.VCC, 74HC165.VCC, C1.+, S1.Pin_3, S1.Pin_4, S2.Pin_3, S2.Pin_4, S3.Pin_3, S3.Pin_4, S4.Pin_3, S4.Pin_4, S5.Pin_3, S5.Pin_4, S6.Pin_3, S6.Pin_4, S7.Pin_3, S7.Pin_4, S8.Pin_3, S8.Pin_4, out_5V.pin1, in_5V.pin1, entradas_sinal.pin9
  N9: 74HC595.SH_CP, in_shif.pin3, out_shift.pin3
  N10: 74HC595.ST_CP, in_shif.pin2, out_shift.pin2
  N11: 74HC595.DS, in_shif.pin1
  N12: 74HC595.Q0, LED1.anode, R9.Pin_1
  N13: Q1.E, O/0.pin1
  N14: Q1.B, R9.Pin_0
  12V: Q1.C, In_12V.pin1, Q9.C, Q10.C, Q11.C, Q12.C, Q13.C, Q14.C, Q15.C, Out_12V.pin1
  N15: LED1.cathode, R1.Pin_1
  N16: LED2.cathode, R2.Pin_1
  N17: LED4.cathode, R4.Pin_1
  N18: LED5.cathode, R5.Pin_1
  N19: LED6.cathode, R6.Pin_1
  N20: LED8.cathode, R8.Pin_1
  N21: LED7.cathode, R7.Pin_1
  N22: R1.Pin_0, R2.Pin_0, R3.Pin_0, R4.Pin_0, R5.Pin_0, R6.Pin_0, R7.Pin_0, R8.Pin_0, Leds.pin1
  N23: R3.Pin_1, LED3.cathode
  N24: R10.Pin_0, Q9.B
  N25: R11.Pin_0, Q10.B
  N26: R12.Pin_0, Q11.B
  N27: R13.Pin_0, Q12.B
  N28: R14.Pin_0, Q13.B
  N29: R15.Pin_0, Q14.B
  N30: R16.Pin_0, Q15.B
  N31: 74HC165.Q1, D_165.pin2, D_165_2.pin2
  N32: 74HC165.Q2, D_165.pin3, D_165_2.pin3
  N33: 74HC165.Q3, R21.Pin_0, S5.Pin_1, S5.Pin_2, entradas_sinal.pin5
  N34: 74HC165.Q4, R22.Pin_0, S6.Pin_1, S6.Pin_2, entradas_sinal.pin6
  N35: 74HC165.Q5, R23.Pin_0, S7.Pin_1, S7.Pin_2, entradas_sinal.pin7
  N36: 74HC165.Q6, R24.Pin_0, S8.Pin_1, S8.Pin_2, entradas_sinal.pin8
  N37: 74HC165.Q7, O_165.pin3
  N38: 74HC165.Q7', O_165.pin2
  N39: 74HC165.MR, O_165.pin1
  N40: 74HC165.SH_CP, R17.Pin_0, S1.Pin_1, S1.Pin_2, entradas_sinal.pin1
  N41: 74HC165.ST_CP, R18.Pin_0, S2.Pin_1, S2.Pin_2, entradas_sinal.pin2
  N42: 74HC165.OE, R19.Pin_0, S3.Pin_1, S3.Pin_2, entradas_sinal.pin3
  N43: 74HC165.DS, R20.Pin_0, S4.Pin_1, S4.Pin_2, entradas_sinal.pin4
  N44: 74HC165.Q0, D_165.pin1, D_165_2.pin1
  N45: Q9.E, O/1.pin1
  N46: Q10.E, O/2.pin1
  N47: Q11.E, O/3.pin1
  N48: Q12.E, O/4.pin1
  N49: Q13.E, O/5.pin1
  N50: Q14.E, O/6.pin1
  N51: Q15.E, O/7.pin1
  N52: D_166.pin1, 74HC596.Q0, D_167.pin1
  N53: D_166.pin2, 74HC596.Q1, D_167.pin2
  N54: D_166.pin3, 74HC596.Q2, D_167.pin3
  N55: R25.Pin_0, S9.Pin_1, S9.Pin_2, 74HC596.Q6, entradas_sinal1.pin8
  GND_2: R25.Pin_1, R26.Pin_1, R27.Pin_1, R28.Pin_1, R29.Pin_1, R30.Pin_1, R31.Pin_1, R32.Pin_1, C2.-, 74HC596.GND, 74HC597.GND, 74HC597.OE, Leds1.pin2, O/8.pin2, O/9.pin2, O/10.pin2, O/11.pin2, O/12.pin2, O/13.pin2, O/14.pin2, O/15.pin2, out_5V1.pin2, Out_12V1.pin2, In_12V1.pin2, in_5V1.pin2
  N56: R26.Pin_0, S10.Pin_1, S10.Pin_2, 74HC596.Q5, entradas_sinal1.pin7
  N57: R27.Pin_0, S11.Pin_1, S11.Pin_2, 74HC596.Q4, entradas_sinal1.pin6
  N58: R28.Pin_0, S12.Pin_1, S12.Pin_2, 74HC596.Q3, entradas_sinal1.pin5
  N59: R29.Pin_0, S13.Pin_1, S13.Pin_2, 74HC596.DS, entradas_sinal1.pin4
  N60: R30.Pin_0, S14.Pin_1, S14.Pin_2, 74HC596.OE, entradas_sinal1.pin3
  N61: R31.Pin_0, S15.Pin_1, S15.Pin_2, 74HC596.ST_CP, entradas_sinal1.pin2
  N62: R32.Pin_0, S16.Pin_1, S16.Pin_2, 74HC596.SH_CP, entradas_sinal1.pin1
  VCC: C2.+, S9.Pin_3, S9.Pin_4, S10.Pin_3, S10.Pin_4, S11.Pin_3, S11.Pin_4, S12.Pin_3, S12.Pin_4, S13.Pin_3, S13.Pin_4, S14.Pin_3, S14.Pin_4, S15.Pin_3, S15.Pin_4, S16.Pin_3, S16.Pin_4, 74HC596.VCC, 74HC597.MR, 74HC597.VCC, out_5V1.pin1, in_5V1.pin1, entradas_sinal1.pin9
  N63: 74HC596.Q7, O_166.pin3
  N64: 74HC596.Q7', O_166.pin2
  N65: 74HC596.MR, O_166.pin1
  N66: 74HC597.Q1, LED15.anode, R47.Pin_1
  N67: 74HC597.Q2, LED14.anode, R46.Pin_1
  N68: 74HC597.Q3, LED13.anode, R45.Pin_1
  N69: 74HC597.Q4, LED12.anode, R44.Pin_1
  N70: 74HC597.Q5, LED11.anode, R43.Pin_1
  N71: 74HC597.Q6, LED9.anode, R42.Pin_1
  N72: 74HC597.Q7, LED10.anode, R41.Pin_1
  N73: 74HC597.Q7', out_shift1.pin1
  N74: 74HC597.SH_CP, out_shift1.pin3, in_shif1.pin3
  N75: 74HC597.ST_CP, out_shift1.pin2, in_shif1.pin2
  N76: 74HC597.DS, in_shif1.pin1
  N77: 74HC597.Q0, LED16.anode, R48.Pin_1
  N78: Q16.E, O/8.pin1
  N79: Q16.B, R41.Pin_0
  N80: Q16.C, Q17.C, Q18.C, Q19.C, Q20.C, Q21.C, Q22.C, Q23.C, Out_12V1.pin1, In_12V1.pin1
  N81: Q17.E, O/9.pin1
  N82: Q17.B, R42.Pin_0
  N83: Q18.E, O/10.pin1
  N84: Q18.B, R43.Pin_0
  N85: Q19.E, O/11.pin1
  N86: Q19.B, R44.Pin_0
  N87: Q20.E, O/12.pin1
  N88: Q20.B, R45.Pin_0
  N89: Q21.E, O/13.pin1
  N90: Q21.B, R46.Pin_0
  N91: Q22.E, O/14.pin1
  N92: Q22.B, R47.Pin_0
  N93: Q23.E, O/15.pin1
  N94: Q23.B, R48.Pin_0
  N95: Leds1.pin1, R33.Pin_0, R34.Pin_0, R35.Pin_0, R36.Pin_0, R37.Pin_0, R38.Pin_0, R39.Pin_0, R40.Pin_0
  N96: LED9.cathode, R34.Pin_1
  N97: LED10.cathode, R33.Pin_1
  N98: LED11.cathode, R35.Pin_1
  N99: LED12.cathode, R36.Pin_1
  N100: LED13.cathode, R37.Pin_1
  N101: LED14.cathode, R38.Pin_1
  N102: LED15.cathode, R39.Pin_1
  N103: LED16.cathode, R40.Pin_1
  N104: D_168.pin1, 74HC598.Q0, D_170.pin1
  N105: D_168.pin2, 74HC598.Q1, D_170.pin2
  N106: D_168.pin3, 74HC598.Q2, D_170.pin3
  N107: D_169.pin1, 74HC599.Q0, D_171.pin1
  N108: D_169.pin2, 74HC599.Q1, D_171.pin2
  N109: D_169.pin3, 74HC599.Q2, D_171.pin3
  N110: R49.Pin_0, S17.Pin_1, S17.Pin_2, 74HC598.Q6, entradas_sinal2.pin8
  GND_3: R49.Pin_1, R51.Pin_1, R53.Pin_1, R55.Pin_1, R57.Pin_1, R59.Pin_1, R61.Pin_1, R63.Pin_1, C3.-, 74HC598.GND, 74HC600.GND, 74HC600.OE, Leds2.pin2, O/16.pin2, O/18.pin2, O/20.pin2, O/22.pin2, O/24.pin2, O/26.pin2, O/28.pin2, O/30.pin2, out_5V2.pin2, Out_12V2.pin2, In_12V2.pin2, in_5V2.pin2
  N111: R50.Pin_0, S18.Pin_1, S18.Pin_2, 74HC599.Q6, entradas_sinal3.pin8
  GND_4: R50.Pin_1, R52.Pin_1, R54.Pin_1, R56.Pin_1, R58.Pin_1, R60.Pin_1, R62.Pin_1, R64.Pin_1, C4.-, 74HC599.GND, 74HC601.GND, 74HC601.OE, Leds3.pin2, O/17.pin2, O/19.pin2, O/21.pin2, O/23.pin2, O/25.pin2, O/27.pin2, O/29.pin2, O/31.pin2, out_5V3.pin2, Out_12V3.pin2, In_12V3.pin2, in_5V3.pin2
  N112: R51.Pin_0, S19.Pin_1, S19.Pin_2, 74HC598.Q5, entradas_sinal2.pin7
  N113: R52.Pin_0, S20.Pin_1, S20.Pin_2, 74HC599.Q5, entradas_sinal3.pin7
  N114: R53.Pin_0, S21.Pin_1, S21.Pin_2, 74HC598.Q4, entradas_sinal2.pin6
  N115: R54.Pin_0, S22.Pin_1, S22.Pin_2, 74HC599.Q4, entradas_sinal3.pin6
  N116: R55.Pin_0, S23.Pin_1, S23.Pin_2, 74HC598.Q3, entradas_sinal2.pin5
  N117: R56.Pin_0, S24.Pin_1, S24.Pin_2, 74HC599.Q3, entradas_sinal3.pin5
  N118: R57.Pin_0, S25.Pin_1, S25.Pin_2, 74HC598.DS, entradas_sinal2.pin4
  N119: R58.Pin_0, S26.Pin_1, S26.Pin_2, 74HC599.DS, entradas_sinal3.pin4
  N120: R59.Pin_0, S27.Pin_1, S27.Pin_2, 74HC598.OE, entradas_sinal2.pin3
  N121: R60.Pin_0, S28.Pin_1, S28.Pin_2, 74HC599.OE, entradas_sinal3.pin3
  N122: R61.Pin_0, S29.Pin_1, S29.Pin_2, 74HC598.ST_CP, entradas_sinal2.pin2
  N123: R62.Pin_0, S30.Pin_1, S30.Pin_2, 74HC599.ST_CP, entradas_sinal3.pin2
  N124: R63.Pin_0, S31.Pin_1, S31.Pin_2, 74HC598.SH_CP, entradas_sinal2.pin1
  N125: R64.Pin_0, S32.Pin_1, S32.Pin_2, 74HC599.SH_CP, entradas_sinal3.pin1
  VCC_2: C3.+, S17.Pin_3, S17.Pin_4, S19.Pin_3, S19.Pin_4, S21.Pin_3, S21.Pin_4, S23.Pin_3, S23.Pin_4, S25.Pin_3, S25.Pin_4, S27.Pin_3, S27.Pin_4, S29.Pin_3, S29.Pin_4, S31.Pin_3, S31.Pin_4, 74HC598.VCC, 74HC600.MR, 74HC600.VCC, out_5V2.pin1, in_5V2.pin1, entradas_sinal2.pin9
  VCC_3: C4.+, S18.Pin_3, S18.Pin_4, S20.Pin_3, S20.Pin_4, S22.Pin_3, S22.Pin_4, S24.Pin_3, S24.Pin_4, S26.Pin_3, S26.Pin_4, S28.Pin_3, S28.Pin_4, S30.Pin_3, S30.Pin_4, S32.Pin_3, S32.Pin_4, 74HC599.VCC, 74HC601.MR, 74HC601.VCC, out_5V3.pin1, in_5V3.pin1, entradas_sinal3.pin9
  N126: 74HC598.Q7, O_167.pin3
  N127: 74HC598.Q7', O_167.pin2
  N128: 74HC598.MR, O_167.pin1
  N129: 74HC599.Q7, O_168.pin3
  N130: 74HC599.Q7', O_168.pin2
  N131: 74HC599.MR, O_168.pin1
  N132: 74HC600.Q1, LED29.anode, R93.Pin_1
  N133: 74HC600.Q2, LED27.anode, R91.Pin_1
  N134: 74HC600.Q3, LED25.anode, R89.Pin_1
  N135: 74HC600.Q4, LED23.anode, R87.Pin_1
  N136: 74HC600.Q5, LED21.anode, R85.Pin_1
  N137: 74HC600.Q6, LED17.anode, R83.Pin_1
  N138: 74HC600.Q7, LED19.anode, R81.Pin_1
  N139: 74HC600.Q7', out_shift2.pin1
  N140: 74HC600.SH_CP, out_shift2.pin3, in_shif2.pin3
  N141: 74HC600.ST_CP, out_shift2.pin2, in_shif2.pin2
  N142: 74HC600.DS, in_shif2.pin1
  N143: 74HC600.Q0, LED31.anode, R95.Pin_1
  N144: 74HC601.Q1, LED30.anode, R94.Pin_1
  N145: 74HC601.Q2, LED28.anode, R92.Pin_1
  N146: 74HC601.Q3, LED26.anode, R90.Pin_1
  N147: 74HC601.Q4, LED24.anode, R88.Pin_1
  N148: 74HC601.Q5, LED22.anode, R86.Pin_1
  N149: 74HC601.Q6, LED18.anode, R84.Pin_1
  N150: 74HC601.Q7, LED20.anode, R82.Pin_1
  N151: 74HC601.Q7', out_shift3.pin1
  N152: 74HC601.SH_CP, out_shift3.pin3, in_shif3.pin3
  N153: 74HC601.ST_CP, out_shift3.pin2, in_shif3.pin2
  N154: 74HC601.DS, in_shif3.pin1
  N155: 74HC601.Q0, LED32.anode, R96.Pin_1
  N156: Q24.E, O/16.pin1
  N157: Q24.B, R81.Pin_0
  N158: Q24.C, Q26.C, Q28.C, Q30.C, Q32.C, Q34.C, Q36.C, Q38.C, Out_12V2.pin1, In_12V2.pin1
  N159: Q25.E, O/17.pin1
  N160: Q25.B, R82.Pin_0
  N161: Q25.C, Q27.C, Q29.C, Q31.C, Q33.C, Q35.C, Q37.C, Q39.C, Out_12V3.pin1, In_12V3.pin1
  N162: Q26.E, O/18.pin1
  N163: Q26.B, R83.Pin_0
  N164: Q27.E, O/19.pin1
  N165: Q27.B, R84.Pin_0
  N166: Q28.E, O/20.pin1
  N167: Q28.B, R85.Pin_0
  N168: Q29.E, O/21.pin1
  N169: Q29.B, R86.Pin_0
  N170: Q30.E, O/22.pin1
  N171: Q30.B, R87.Pin_0
  N172: Q31.E, O/23.pin1
  N173: Q31.B, R88.Pin_0
  N174: Q32.E, O/24.pin1
  N175: Q32.B, R89.Pin_0
  N176: Q33.E, O/25.pin1
  N177: Q33.B, R90.Pin_0
  N178: Q34.E, O/26.pin1
  N179: Q34.B, R91.Pin_0
  N180: Q35.E, O/27.pin1
  N181: Q35.B, R92.Pin_0
  N182: Q36.E, O/28.pin1
  N183: Q36.B, R93.Pin_0
  N184: Q37.E, O/29.pin1
  N185: Q37.B, R94.Pin_0
  N186: Q38.E, O/30.pin1
  N187: Q38.B, R95.Pin_0
  N188: Q39.E, O/31.pin1
  N189: Q39.B, R96.Pin_0
  N190: Leds2.pin1, R65.Pin_0, R67.Pin_0, R69.Pin_0, R71.Pin_0, R73.Pin_0, R75.Pin_0, R77.Pin_0, R79.Pin_0
  N191: Leds3.pin1, R66.Pin_0, R68.Pin_0, R70.Pin_0, R72.Pin_0, R74.Pin_0, R76.Pin_0, R78.Pin_0, R80.Pin_0
  N192: LED17.cathode, R67.Pin_1
  N193: LED18.cathode, R68.Pin_1
  N194: LED19.cathode, R65.Pin_1
  N195: LED20.cathode, R66.Pin_1
  N196: LED21.cathode, R69.Pin_1
  N197: LED22.cathode, R70.Pin_1
  N198: LED23.cathode, R71.Pin_1
  N199: LED24.cathode, R72.Pin_1
  N200: LED25.cathode, R73.Pin_1
  N201: LED26.cathode, R74.Pin_1
  N202: LED27.cathode, R75.Pin_1
  N203: LED28.cathode, R76.Pin_1
  N204: LED29.cathode, R77.Pin_1
  N205: LED30.cathode, R78.Pin_1
  N206: LED31.cathode, R79.Pin_1
  N207: LED32.cathode, R80.Pin_1
