# Fritzing sketch 74hc595_expandido_adapt (saved by Fritzing 0.9.4)
circuit board: 20cm x 15cm
breadboards: 1

parts:
  74HC595 = 74HC595 [package="DIP16 [THT]"]
  Q1 = NPN-Transistor [package="TO92 [THT]"]
  LED1 = LED - 5mm [color="Red (633nm)" package="5 mm [THT]"]
  LED2 = LED - 5mm [color="Red (633nm)" package="5 mm [THT]"]
  LED4 = LED - 5mm [color="Red (633nm)" package="5 mm [THT]"]
  LED5 = LED - 5mm [color="Red (633nm)" package="5 mm [THT]"]
  LED6 = LED - 5mm [color="Red (633nm)" package="5 mm [THT]"]
  LED8 = LED - 5mm [color="Red (633nm)" package="5 mm [THT]"]
  LED7 = LED - 5mm [color="Red (633nm)" package="5 mm [THT]"]
  R1 = Resistor [tolerance=±5% resistance=220 package=THT]
  R2 = Resistor [tolerance=±5% resistance=220 package=THT]
  R3 = Resistor [tolerance=±5% resistance=220 package=THT]
  R4 = Resistor [tolerance=±5% resistance=220 package=THT]
  R5 = Resistor [tolerance=±5% resistance=220 package=THT]
  R6 = Resistor [tolerance=±5% resistance=220 package=THT]
  R7 = Resistor [tolerance=±5% resistance=220 package=THT]
  R8 = Resistor [tolerance=±5% resistance=220 package=THT]
  R9 = Resistor [tolerance=±5% resistance=4.7k package=THT]
  R10 = Resistor [tolerance=±5% resistance=4.7k package=THT]
  R11 = Resistor [tolerance=±5% resistance=4.7k package=THT]
  R12 = Resistor [tolerance=±5% resistance=4.7k package=THT]
  R13 = Resistor [tolerance=±5% resistance=4.7k package=THT]
  R14 = Resistor [tolerance=±5% resistance=4.7k package=THT]
  R15 = Resistor [tolerance=±5% resistance=4.7k package=THT]
  R16 = Resistor [tolerance=±5% resistance=4.7k package=THT]
  In_12V = male pin header, 2 pins [form="♂ (male)"]
  74HC165 = 74HC595 [package="DIP16 [THT]"]
  R17 = Resistor [tolerance=±5% resistance=10k package=THT]
  R18 = Resistor [tolerance=±5% resistance=10k package=THT]
  R19 = Resistor [tolerance=±5% resistance=10k package=THT]
  R20 = Resistor [tolerance=±5% resistance=10k package=THT]
  R21 = Resistor [tolerance=±5% resistance=10k package=THT]
  R22 = Resistor [tolerance=±5% resistance=10k package=THT]
  R23 = Resistor [tolerance=±5% resistance=10k package=THT]
  R24 = Resistor [tolerance=±5% resistance=10k package=THT]
  C1 = Electrolytic Capacitor [capacitance=0.1mF package="100 mil [THT, electrolytic]"]
  S1 = Pushbutton [package="[THT]"]
  S2 = Pushbutton [package="[THT]"]
  S3 = Pushbutton [package="[THT]"]
  S4 = Pushbutton [package="[THT]"]
  S5 = Pushbutton [package="[THT]"]
  S6 = Pushbutton [package="[THT]"]
  S7 = Pushbutton [package="[THT]"]
  S8 = Pushbutton [package="[THT]"]
  LED3 = LED - 5mm [color="Red (633nm)" package="5 mm [THT]"]
  Q9 = NPN-Transistor [package="TO92 [THT]"]
  Q10 = NPN-Transistor [package="TO92 [THT]"]
  Q11 = NPN-Transistor [package="TO92 [THT]"]
  Q12 = NPN-Transistor [package="TO92 [THT]"]
  Q13 = NPN-Transistor [package="TO92 [THT]"]
  Q14 = NPN-Transistor [package="TO92 [THT]"]
  Q15 = NPN-Transistor [package="TO92 [THT]"]
  D_165 = male pin header, 3 pins [form="♂ (male)"]
  O/7 = female pin header, 2 pins [form="♀ (female)"]
  O/5 = female pin header, 2 pins [form="♀ (female)"]
  O/6 = female pin header, 2 pins [form="♀ (female)"]
  O/4 = female pin header, 2 pins [form="♀ (female)"]
  O/3 = female pin header, 2 pins [form="♀ (female)"]
  O/2 = female pin header, 2 pins [form="♀ (female)"]
  O/1 = female pin header, 2 pins [form="♀ (female)"]
  O/0 = female pin header, 2 pins [form="♀ (female)"]
  in_5V = male pin header, 2 pins [form="♂ (male)"]
  in_shif = male pin header, 3 pins [form="♂ (male)"]
  out_shift = male pin header, 3 pins [form="♂ (male)"]
  Leds = male pin header, 2 pins [form="♂ (male)"]
  O_165 = female pin header, 3 pins [form="♀ (female)"]
  D_166 = male pin header, 3 pins [form="♂ (male)"]
  R25 = Resistor [tolerance=±5% resistance=10k package=THT]
  R26 = Resistor [tolerance=±5% resistance=10k package=THT]
  R27 = Resistor [tolerance=±5% resistance=10k package=THT]
  R28 = Resistor [tolerance=±5% resistance=10k package=THT]
  R29 = Resistor [tolerance=±5% resistance=10k package=THT]
  R30 = Resistor [tolerance=±5% resistance=10k package=THT]
  R31 = Resistor [tolerance=±5% resistance=10k package=THT]
  R32 = Resistor [tolerance=±5% resistance=10k package=THT]
  C2 = Electrolytic Capacitor [capacitance=0.1mF package="100 mil [THT, electrolytic]"]
  S9 = Pushbutton [package="[THT]"]
  S10 = Pushbutton [package="[THT]"]
  S11 = Pushbutton [package="[THT]"]
  S12 = Pushbutton [package="[THT]"]
  S13 = Pushbutton [package="[THT]"]
  S14 = Pushbutton [package="[THT]"]
  S15 = Pushbutton [package="[THT]"]
  S16 = Pushbutton [package="[THT]"]
  74HC596 = 74HC595 [package="DIP16 [THT]"]
  74HC597 = 74HC595 [package="DIP16 [THT]"]
  Q16 = NPN-Transistor [package="TO92 [THT]"]
  Q17 = NPN-Transistor [package="TO92 [THT]"]
  Q18 = NPN-Transistor [package="TO92 [THT]"]
  Q19 = NPN-Transistor [package="TO92 [THT]"]
  Q20 = NPN-Transistor [package="TO92 [THT]"]
  Q21 = NPN-Transistor [package="TO92 [THT]"]
  Q22 = NPN-Transistor [package="TO92 [THT]"]
  Q23 = NPN-Transistor [package="TO92 [THT]"]
  Leds1 = male pin header, 2 pins [form="♂ (male)"]
  O/8 = female pin header, 2 pins [form="♀ (female)"]
  O/9 = female pin header, 2 pins [form="♀ (female)"]
  O/10 = female pin header, 2 pins [form="♀ (female)"]
  O/11 = female pin header, 2 pins [form="♀ (female)"]
  O/12 = female pin header, 2 pins [form="♀ (female)"]
  O/13 = female pin header, 2 pins [form="♀ (female)"]
  O/14 = female pin header, 2 pins [form="♀ (female)"]
  O/15 = female pin header, 2 pins [form="♀ (female)"]
  out_shift1 = male pin header, 3 pins [form="♂ (male)"]
  O_166 = female pin header, 3 pins [form="♀ (female)"]
  D_167 = female pin header, 3 pins [form="♀ (female)"]
  in_shif1 = male pin header, 3 pins [form="♂ (male)"]
  Out_12V1 = male pin header, 2 pins [form="♂ (male)"]
  In_12V1 = male pin header, 2 pins [form="♂ (male)"]
  LED9 = LED - 5mm [color="Red (633nm)" package="5 mm [THT]"]
  LED10 = LED - 5mm [color="Red (633nm)" package="5 mm [THT]"]
  LED11 = LED - 5mm [color="Red (633nm)" package="5 mm [THT]"]
  LED12 = LED - 5mm [color="Red (633nm)" package="5 mm [THT]"]
  LED13 = LED - 5mm [color="Red (633nm)" package="5 mm [THT]"]
  LED14 = LED - 5mm [color="Red (633nm)" package="5 mm [THT]"]
  LED15 = LED - 5mm [color="Red (633nm)" package="5 mm [THT]"]
  LED16 = LED - 5mm [color="Red (633nm)" package="5 mm [THT]"]
  R33 = Resistor [tolerance=±5% resistance=220 package=THT]
  R34 = Resistor [tolerance=±5% resistance=220 package=THT]
  R35 = Resistor [tolerance=±5% resistance=220 package=THT]
  R36 = Resistor [tolerance=±5% resistance=220 package=THT]
  R37 = Resistor [tolerance=±5% resistance=220 package=THT]
  R38 = Resistor [tolerance=±5% resistance=220 package=THT]
  R39 = Resistor [tolerance=±5% resistance=220 package=THT]
  R40 = Resistor [tolerance=±5% resistance=220 package=THT]
  R41 = Resistor [tolerance=±5% resistance=4.7k package=THT]
  R42 = Resistor [tolerance=±5% resistance=4.7k package=THT]
  R43 = Resistor [tolerance=±5% resistance=4.7k package=THT]
  R44 = Resistor [tolerance=±5% resistance=4.7k package=THT]
  R45 = Resistor [tolerance=±5% resistance=4.7k package=THT]
  R46 = Resistor [tolerance=±5% resistance=4.7k package=THT]
  R47 = Resistor [tolerance=±5% resistance=4.7k package=THT]
  R48 = Resistor [tolerance=±5% resistance=4.7k package=THT]
  entradas_sinal = male pin header, 9 pins [form="♂ (male)"]
  entradas_sinal1 = male pin header, 9 pins [form="♂ (male)"]

nets:
  N1: 74HC595.Q1, LED2.anode, R10.Pin_1
  N2: 74HC595.Q2, R11.Pin_1, LED3.anode
  N3: 74HC595.Q3, LED4.anode, R12.Pin_1
  N4: 74HC595.Q4, LED5.anode, R13.Pin_1
  N5: 74HC595.Q5, LED6.anode, R14.Pin_1
  N6: 74HC595.Q6, LED7.anode, R15.Pin_1
  N7: 74HC595.Q7, LED8.anode, R16.Pin_1
  GND: 74HC595.GND, 74HC595.OE, In_12V.pin2, 74HC165.GND, R17.Pin_1, R18.Pin_1, R19.Pin_1, R20.Pin_1, R21.Pin_1, R22.Pin_1, R23.Pin_1, R24.Pin_1, C1.-, O/7.pin2, O/5.pin2, O/6.pin2, O/4.pin2, O/3.pin2, O/2.pin2, O/1.pin2, O/0.pin2, in_5V.pin2, Leds.pin2, R25.Pin_1, R26.Pin_1, R27.Pin_1, R28.Pin_1, R29.Pin_1, R30.Pin_1, R31.Pin_1, R32.Pin_1, C2.-, 74HC596.GND, 74HC597.GND, 74HC597.OE, Leds1.pin2, O/8.pin2, O/9.pin2, O/10.pin2, O/11.pin2, O/12.pin2, O/13.pin2, O/14.pin2, O/15.pin2, Out_12V1.pin2, In_12V1.pin2
  N8: 74HC595.Q7', out_shift.pin1
  5V: 74HC595.MR, 74HC595.VCC, 74HC165.VCC, C1.+, S1.Pin_3, S1.Pin_4, S2.Pin_3, S2.Pin_4, S3.Pin_3, S3.Pin_4, S4.Pin_3, S4.Pin_4, S5.Pin_3, S5.Pin_4, S6.Pin_3, S6.Pin_4, S7.Pin_3, S7.Pin_4, S8.Pin_3, S8.Pin_4, in_5V.pin1, C2.+, S9.Pin_3, S9.Pin_4, S10.Pin_3, S10.Pin_4, S11.Pin_3, S11.Pin_4, S12.Pin_3, S12.Pin_4, S13.Pin_3, S13.Pin_4, S14.Pin_3, S14.Pin_4, S15.Pin_3, S15.Pin_4, S16.Pin_4, 74HC596.VCC, 74HC597.MR, 74HC597.VCC, entradas_sinal.pin9, entradas_sinal1.pin9
  N9: 74HC595.SH_CP, in_shif.pin3, out_shift.pin3
  N10: 74HC595.ST_CP, in_shif.pin2, out_shift.pin2
  N11: 74HC595.DS, in_shif.pin1
  N12: 74HC595.Q0, LED1.anode, R9.Pin_1
  N13: Q1.E, O/0.pin1
  N14: Q1.B, R9.Pin_0
  12V: Q1.C, In_12V.pin1, Q9.C, Q10.C, Q11.C, Q12.C, Q13.C, Q14.C, Q15.C, Q16.C, Q17.C, Q18.C, Q19.C, Q20.C, Q21.C, Q22.C, Q23.C, Out_12V1.pin1, In_12V1.pin1
  N15: LED1.cathode, R1.Pin_1
  N16: LED2.cathode, R2.Pin_1
  N17: LED4.cathode, R4.Pin_1
  N18: LED5.cathode, R5.Pin_1
  N19: LED6.cathode, R6.Pin_1
  N20: LED8.cathode, R8.Pin_1
  N21: LED7.cathode, R7.Pin_1
  N22: R1.Pin_0, R2.Pin_0, R3.Pin_0, R4.Pin_0, R5.Pin_0, R6.Pin_0, R7.Pin_0, R8.Pin_0, Leds.pin1
  N23: R3.Pin_1, LED3.cathode
  N24: R10.Pin_0, Q9.B
  N25: R11.Pin_0, Q10.B
  N26: R12.Pin_0, Q11.B
  N27: R13.Pin_0, Q12.B
  N28: R14.Pin_0, Q13.B
  N29: R15.Pin_0, Q14.B
  N30: R16.Pin_0, Q15.B
  N31: 74HC165.Q1, D_165.pin2
  N32: 74HC165.Q2, D_165.pin3
  N33: 74HC165.Q3, R21.Pin_0, S5.Pin_1, S5.Pin_2, entradas_sinal.pin5
  N34: 74HC165.Q4, R22.Pin_0, S6.Pin_1, S6.Pin_2, entradas_sinal.pin6
  N35: 74HC165.Q5, R23.Pin_0, S7.Pin_1, S7.Pin_2, entradas_sinal.pin7
  N36: 74HC165.Q6, R24.Pin_0, S8.Pin_1, S8.Pin_2, entradas_sinal.pin8
  N37: 74HC165.Q7, O_165.pin3
  N38: 74HC165.Q7', O_165.pin2
  N39: 74HC165.MR, O_165.pin1
  N40: 74HC165.SH_CP, R17.Pin_0, S1.Pin_1, S1.Pin_2, entradas_sinal.pin1
  N41: 74HC165.ST_CP, R18.Pin_0, S2.Pin_1, S2.Pin_2, entradas_sinal.pin2
  N42: 74HC165.OE, R19.Pin_0, S3.Pin_1, S3.Pin_2, entradas_sinal.pin3
  N43: 74HC165.DS, R20.Pin_0, S4.Pin_1, S4.Pin_2, entradas_sinal.pin4
  N44: 74HC165.Q0, D_165.pin1
  N45: Q9.E, O/1.pin1
  N46: Q10.E, O/2.pin1
  N47: Q11.E, O/3.pin1
  N48: Q12.E, O/4.pin1
  N49: Q13.E, O/5.pin1
  N50: Q14.E, O/6.pin1
  N51: Q15.E, O/7.pin1
  N52: D_166.pin1, 74HC596.Q0, D_167.pin1
  N53: D_166.pin2, 74HC596.Q1, D_167.pin2
  N54: D_166.pin3, 74HC596.Q2, D_167.pin3
  N55: R25.Pin_0, S9.Pin_1, S9.Pin_2, 74HC596.Q6, entradas_sinal1.pin8
  N56: R26.Pin_0, S10.Pin_1, S10.Pin_2, 74HC596.Q5, entradas_sinal1.pin7
  N57: R27.Pin_0, S11.Pin_1, S11.Pin_2, 74HC596.Q4, entradas_sinal1.pin6
  N58: R28.Pin_0, S12.Pin_1, S12.Pin_2, 74HC596.Q3, entradas_sinal1.pin5
  N59: R29.Pin_0, S13.Pin_1, S13.Pin_2, 74HC596.DS, entradas_sinal1.pin4
  N60: R30.Pin_0, S14.Pin_1, S14.Pin_2, 74HC596.OE, entradas_sinal1.pin3
  N61: R31.Pin_0, S15.Pin_1, S15.Pin_2, 74HC596.ST_CP, entradas_sinal1.pin2
  N62: R32.Pin_0, S16.Pin_1, S16.Pin_2, 74HC596.SH_CP, entradas_sinal1.pin1
  N63: 74HC596.Q7, O_166.pin3
  N64: 74HC596.Q7', O_166.pin2
  N65: 74HC596.MR, O_166.pin1
  N66: 74HC597.Q1, LED15.anode, R47.Pin_1
  N67: 74HC597.Q2, LED14.anode, R46.Pin_1
  N68: 74HC597.Q3, LED13.anode, R45.Pin_1
  N69: 74HC597.Q4, LED12.anode, R44.Pin_1
  N70: 74HC597.Q5, LED11.anode, R43.Pin_1
  N71: 74HC597.Q6, LED9.anode, R42.Pin_1
  N72: 74HC597.Q7, LED10.anode, R41.Pin_1
  N73: 74HC597.Q7', out_shift1.pin1
  N74: 74HC597.SH_CP, out_shift1.pin3, in_shif1.pin3
  N75: 74HC597.ST_CP, out_shift1.pin2, in_shif1.pin2
  N76: 74HC597.DS, in_shif1.pin1
  N77: 74HC597.Q0, LED16.anode, R48.Pin_1
  N78: Q16.E, O/8.pin1
  N79: Q16.B, R41.Pin_0
  N80: Q17.E, O/9.pin1
  N81: Q17.B, R42.Pin_0
  N82: Q18.E, O/10.pin1
  N83: Q18.B, R43.Pin_0
  N84: Q19.E, O/11.pin1
  N85: Q19.B, R44.Pin_0
  N86: Q20.E, O/12.pin1
  N87: Q20.B, R45.Pin_0
  N88: Q21.E, O/13.pin1
  N89: Q21.B, R46.Pin_0
  N90: Q22.E, O/14.pin1
  N91: Q22.B, R47.Pin_0
  N92: Q23.E, O/15.pin1
  N93: Q23.B, R48.Pin_0
  N94: Leds1.pin1, R33.Pin_0, R34.Pin_0, R35.Pin_0, R36.Pin_0, R37.Pin_0, R38.Pin_0, R39.Pin_0, R40.Pin_0
  N95: LED9.cathode, R34.Pin_1
  N96: LED10.cathode, R33.Pin_1
  N97: LED11.cathode, R35.Pin_1
  N98: LED12.cathode, R36.Pin_1
  N99: LED13.cathode, R37.Pin_1
  N100: LED14.cathode, R38.Pin_1
  N101: LED15.cathode, R39.Pin_1
  N102: LED16.cathode, R40.Pin_1
