# Fritzing sketch 74hc595_final2_wifi (saved by Fritzing 0.9.3b)
circuit board: 10cm x 10cm
breadboards: 1

parts:
  74HC595 = 74HC595 [package="DIP16 [THT]"]
  Q1 = NPN-Transistor [package="TO92 [THT]"]
  in_5V = male pin header, 2 pins [form="♂ (male)"]
  LED1 = LED - 5mm [color="Red (633nm)" package="5 mm [THT]"]
  in_shif = male pin header, 3 pins [form="♂ (male)"]
  LED2 = LED - 5mm [color="Red (633nm)" package="5 mm [THT]"]
  LED4 = LED - 5mm [color="Red (633nm)" package="5 mm [THT]"]
  LED5 = LED - 5mm [color="Red (633nm)" package="5 mm [THT]"]
  LED6 = LED - 5mm [color="Red (633nm)" package="5 mm [THT]"]
  LED8 = LED - 5mm [color="Red (633nm)" package="5 mm [THT]"]
  LED7 = LED - 5mm [color="Red (633nm)" package="5 mm [THT]"]
  R1 = Resistor [tolerance=±5% resistance=470 package=THT]
  R3 = Resistor [tolerance=±5% resistance=220 package=THT]
  R4 = Resistor [tolerance=±10% resistance=220 package=THT]
  R5 = Resistor [tolerance=±5% resistance=220 package=THT]
  R6 = Resistor [tolerance=±5% resistance=220 package=THT]
  R7 = Resistor [tolerance=±5% resistance=220 package=THT]
  R8 = Resistor [tolerance=±5% resistance=330 package=THT]
  Leds = male pin header, 2 pins [form="♂ (male)"]
  R9 = Resistor [tolerance=±5% resistance=220k package=THT]
  In_12V = male pin header, 2 pins [form="♂ (male)"]
  74HC165 = 74HC595 [package="DIP16 [THT]"]
  R24 = Resistor [tolerance=±5% resistance=10k package=THT]
  R23 = Resistor [tolerance=±5% resistance=10k package=THT]
  R22 = Resistor [tolerance=±5% resistance=10k package=THT]
  R21 = Resistor [tolerance=±5% resistance=10k package=THT]
  R20 = Resistor [tolerance=±5% resistance=10k package=THT]
  R19 = Resistor [tolerance=±20% resistance=10k package=THT]
  R18 = Resistor [tolerance=±20% resistance=10k package=THT]
  R17 = Resistor [tolerance=±5% resistance=15k package=THT]
  S8 = Pushbutton [package="[THT]"]
  S7 = Pushbutton [package="[THT]"]
  S6 = Pushbutton [package="[THT]"]
  S5 = Pushbutton [package="[THT]"]
  S4 = Pushbutton [package="[THT]"]
  S3 = Pushbutton [package="[THT]"]
  S2 = Pushbutton [package="[THT]"]
  S1 = Pushbutton [package="[THT]"]
  out_shift = male pin header, 3 pins [form="♂ (male)"]
  out_5V = male pin header, 2 pins [form="♂ (male)"]
  LED3 = LED - 5mm [color="Red (633nm)" package="5 mm [THT]"]
  O/0 = female pin header, 2 pins [form="♀ (female)"]
  Out_12V = male pin header, 2 pins [form="♂ (male)"]
  D_165 = female pin header, 3 pins [form="♀ (female)"]
  O_165 = female pin header, 3 pins [form="♀ (female)"]
  D_165_2 = male pin header, 3 pins [form="♂ (male)"]
  Q2 = PNP-Transistor [package="TO92 [THT]"]
  R25 = Resistor [tolerance=±5% resistance=100k package=THT]
  Q3 = NPN-Transistor [package="TO92 [THT]"]
  O/8 = female pin header, 2 pins [form="♀ (female)"]
  R10 = Resistor [tolerance=±5% resistance=100k package=THT]
  R26 = Resistor [tolerance=±20% resistance=330k package=THT]
  Q4 = PNP-Transistor [package="TO92 [THT]"]
  Q5 = NPN-Transistor [package="TO92 [THT]"]
  O/9 = female pin header, 2 pins [form="♀ (female)"]
  R27 = Resistor [tolerance=±5% resistance=100k package=THT]
  Q6 = PNP-Transistor [package="TO92 [THT]"]
  Q7 = NPN-Transistor [package="TO92 [THT]"]
  O/10 = female pin header, 2 pins [form="♀ (female)"]
  R12 = Resistor [tolerance=±5% resistance=100k package=THT]
  R28 = Resistor [tolerance=±5% resistance=100k package=THT]
  Q8 = PNP-Transistor [package="TO92 [THT]"]
  Q9 = NPN-Transistor [package="TO92 [THT]"]
  O/11 = female pin header, 2 pins [form="♀ (female)"]
  R13 = Resistor [tolerance=±5% resistance=100k package=THT]
  R29 = Resistor [tolerance=±20% resistance=100k package=THT]
  Q11 = NPN-Transistor [package="TO92 [THT]"]
  O/12 = female pin header, 2 pins [form="♀ (female)"]
  R14 = Resistor [tolerance=±5% resistance=220k package=THT]
  R30 = Resistor [tolerance=±20% resistance=100k package=THT]
  Q12 = PNP-Transistor [package="TO92 [THT]"]
  Q13 = NPN-Transistor [package="TO92 [THT]"]
  O/13 = female pin header, 2 pins [form="♀ (female)"]
  R15 = Resistor [tolerance=±5% resistance=100k package=THT]
  R31 = Resistor [tolerance=±20% resistance=150k package=THT]
  Q14 = PNP-Transistor [package="TO92 [THT]"]
  Q15 = NPN-Transistor [package="TO92 [THT]"]
  O/14 = female pin header, 2 pins [form="♀ (female)"]
  R16 = Resistor [tolerance=±5% resistance=100k package=THT]
  R32 = Resistor [tolerance=±0.05% resistance=100k package=THT]
  Q16 = PNP-Transistor [package="TO92 [THT]"]
  C1 = Electrolytic Capacitor [capacitance=0.1mF package="100 mil [THT, electrolytic]"]
  R2 = Resistor [tolerance=±5% resistance=220 package=THT]
  J96 = female pin header, 1 pin [form="♀ (female)"]  # not connected
  J97 = female pin header, 1 pin [form="♀ (female)"]  # not connected
  J98 = female pin header, 1 pin [form="♀ (female)"]  # not connected
  J99 = female pin header, 1 pin [form="♀ (female)"]  # not connected
  J100 = female pin header, 1 pin [form="♀ (female)"]  # not connected
  J101 = female pin header, 1 pin [form="♀ (female)"]  # not connected
  J102 = female pin header, 1 pin [form="♀ (female)"]  # not connected
  J103 = female pin header, 1 pin [form="♀ (female)"]  # not connected
  J104 = female pin header, 1 pin [form="♀ (female)"]  # not connected
  J105 = female pin header, 1 pin [form="♀ (female)"]  # not connected
  J106 = female pin header, 1 pin [form="♀ (female)"]  # not connected
  J107 = female pin header, 1 pin [form="♀ (female)"]  # not connected
  J108 = female pin header, 1 pin [form="♀ (female)"]  # not connected
  J109 = female pin header, 1 pin [form="♀ (female)"]  # not connected
  J110 = female pin header, 1 pin [form="♀ (female)"]  # not connected
  entradas_sinal = male pin header, 9 pins [form="♂ (male)"]
  Q10 = PNP-Transistor [package="TO92 [THT]"]
  R11 = Resistor [tolerance=±5% resistance=100k package=THT]
  LED9 = LED - 5mm [color="Red (633nm)" package="5 mm [THT]"]
  R33 = Resistor [tolerance=±5% resistance=330 package=THT]
  On/off = male pin header, 2 pins [form="♂ (male)"]
  ESP1 = female pin header, 3 pins [form="♀ (female)"]  # not connected
  ESP2 = female pin header, 3 pins [form="♀ (female)"]  # not connected

nets:
  N1: 74HC595.Q1, R10.Pin_1, R2.Pin_1
  N2: 74HC595.Q2, R3.Pin_1, R11.Pin_1
  N3: 74HC595.Q3, R4.Pin_1, R12.Pin_1
  N4: 74HC595.Q4, R5.Pin_1, R13.Pin_1
  N5: 74HC595.Q5, R6.Pin_1, R14.Pin_1
  N6: 74HC595.Q6, R7.Pin_1, R15.Pin_1
  N7: 74HC595.Q7, R8.Pin_1, R16.Pin_1
  GND: 74HC595.GND, 74HC595.OE, Q1.E, in_5V.pin2, Leds.pin2, In_12V.pin2, 74HC165.GND, R24.Pin_1, R23.Pin_1, R22.Pin_1, R21.Pin_1, R20.Pin_1, R19.Pin_1, R18.Pin_1, R17.Pin_1, out_5V.pin2, O/0.pin2, Out_12V.pin2, Q3.E, O/8.pin2, Q5.E, O/9.pin2, Q7.E, O/10.pin2, Q9.E, O/11.pin2, Q11.E, O/12.pin2, Q13.E, O/13.pin2, Q15.E, O/14.pin2, C1.-, LED9.cathode
  N8: 74HC595.Q7', out_shift.pin1
  5V: 74HC595.MR, 74HC595.VCC, in_5V.pin1, 74HC165.VCC, S8.Pin_3, S8.Pin_4, S7.Pin_3, S7.Pin_4, S6.Pin_3, S6.Pin_4, S5.Pin_3, S5.Pin_4, S4.Pin_3, S4.Pin_4, S3.Pin_3, S3.Pin_4, S2.Pin_3, S2.Pin_4, S1.Pin_3, S1.Pin_4, out_5V.pin1, C1.+, entradas_sinal.pin9, On/off.pin1
  N9: 74HC595.SH_CP, in_shif.pin3, out_shift.pin3
  N10: 74HC595.ST_CP, in_shif.pin2, out_shift.pin2
  N11: 74HC595.DS, in_shif.pin1
  N12: 74HC595.Q0, R1.Pin_1, R9.Pin_1
  N13: Q1.B, R9.Pin_0
  N14: Q1.C, R25.Pin_1
  N15: LED1.cathode, LED2.cathode, LED4.cathode, LED5.cathode, LED6.cathode, LED8.cathode, LED7.cathode, Leds.pin1, LED3.cathode
  N16: LED1.anode, R1.Pin_0
  N17: LED2.anode, R2.Pin_0
  N18: LED4.anode, R4.Pin_0
  N19: LED5.anode, R5.Pin_0
  N20: LED6.anode, R6.Pin_0
  N21: LED8.anode, R8.Pin_0
  N22: LED7.anode, R7.Pin_0
  N23: R3.Pin_0, LED3.anode
  12V: In_12V.pin1, Out_12V.pin1, Q2.E, Q4.E, Q6.E, Q8.E, Q12.E, Q14.E, Q16.E, Q10.E
  N24: 74HC165.Q1, D_165.pin2, D_165_2.pin2
  N25: 74HC165.Q2, D_165.pin3, D_165_2.pin3
  N26: 74HC165.Q3, R20.Pin_0, S4.Pin_1, S4.Pin_2, entradas_sinal.pin4
  N27: 74HC165.Q4, R19.Pin_0, S3.Pin_1, S3.Pin_2, entradas_sinal.pin3
  N28: 74HC165.Q5, R18.Pin_0, S2.Pin_1, S2.Pin_2, entradas_sinal.pin2
  N29: 74HC165.Q6, R17.Pin_0, S1.Pin_1, S1.Pin_2, entradas_sinal.pin1
  N30: 74HC165.Q7, O_165.pin3
  N31: 74HC165.Q7', O_165.pin1
  N32: 74HC165.MR, O_165.pin2
  N33: 74HC165.SH_CP, R24.Pin_0, S8.Pin_1, S8.Pin_2, entradas_sinal.pin8
  N34: 74HC165.ST_CP, R23.Pin_0, S7.Pin_1, S7.Pin_2, entradas_sinal.pin7
  N35: 74HC165.OE, R22.Pin_0, S6.Pin_1, S6.Pin_2, entradas_sinal.pin6
  N36: 74HC165.DS, R21.Pin_0, S5.Pin_1, S5.Pin_2, entradas_sinal.pin5
  N37: 74HC165.Q0, D_165.pin1, D_165_2.pin1
  N38: O/0.pin1, Q2.C
  N39: Q2.B, R25.Pin_0
  N40: Q3.B, R10.Pin_0
  N41: Q3.C, R26.Pin_1
  N42: O/8.pin1, Q4.C
  N43: R26.Pin_0, Q4.B
  N44: Q5.B, R11.Pin_0
  N45: Q5.C, R27.Pin_1
  N46: O/9.pin1, Q6.C
  N47: R27.Pin_0, Q6.B
  N48: Q7.B, R12.Pin_0
  N49: Q7.C, R28.Pin_1
  N50: O/10.pin1, Q8.C
  N51: R28.Pin_0, Q8.B
  N52: Q9.B, R13.Pin_0
  N53: Q9.C, R29.Pin_1
  N54: O/11.pin1, Q10.C
  N55: R29.Pin_0, Q10.B
  N56: Q11.B, R14.Pin_0
  N57: Q11.C, R30.Pin_1
  N58: O/12.pin1, Q12.C
  N59: R30.Pin_0, Q12.B
  N60: Q13.B, R15.Pin_0
  N61: Q13.C, R31.Pin_1
  N62: O/13.pin1, Q14.C
  N63: R31.Pin_0, Q14.B
  N64: Q15.B, R16.Pin_0
  N65: Q15.C, R32.Pin_1
  N66: O/14.pin1, Q16.C
  N67: R32.Pin_0, Q16.B
  N68: LED9.anode, R33.Pin_0
  N69: R33.Pin_1, On/off.pin2
