# Fritzing sketch 74hc595_roteado (saved by Fritzing 0.9.4)
circuit board: 10cm x 7cm
breadboards: 1

parts:
  74HC595 = 74HC595 [package="DIP16 [THT]"]
  Q1 = NPN-Transistor [package="TO92 [THT]"]
  LED1 = LED - 5mm [color="Red (633nm)" package="5 mm [THT]"]
  LED2 = LED - 5mm [color="Red (633nm)" package="5 mm [THT]"]
  LED4 = LED - 5mm [color="Red (633nm)" package="5 mm [THT]"]
  LED5 = LED - 5mm [color="Red (633nm)" package="5 mm [THT]"]
  LED6 = LED - 5mm [color="Red (633nm)" package="5 mm [THT]"]
  LED8 = LED - 5mm [color="Red (633nm)" package="5 mm [THT]"]
  LED7 = LED - 5mm [color="Red (633nm)" package="5 mm [THT]"]
  R1 = Resistor [tolerance=±5% resistance=220 package=THT]
  R2 = Resistor [tolerance=±5% resistance=220 package=THT]
  R3 = Resistor [tolerance=±5% resistance=220 package=THT]
  R4 = Resistor [tolerance=±5% resistance=220 package=THT]
  R5 = Resistor [tolerance=±5% resistance=220 package=THT]
  R6 = Resistor [tolerance=±5% resistance=220 package=THT]
  R7 = Resistor [tolerance=±5% resistance=220 package=THT]
  R8 = Resistor [tolerance=±5% resistance=220 package=THT]
  R9 = Resistor [tolerance=±5% resistance=4.7k package=THT]
  R10 = Resistor [tolerance=±5% resistance=4.7k package=THT]
  R11 = Resistor [tolerance=±5% resistance=4.7k package=THT]
  R12 = Resistor [tolerance=±5% resistance=4.7k package=THT]
  R13 = Resistor [tolerance=±5% resistance=4.7k package=THT]
  R14 = Resistor [tolerance=±5% resistance=4.7k package=THT]
  R15 = Resistor [tolerance=±5% resistance=4.7k package=THT]
  R16 = Resistor [tolerance=±5% resistance=4.7k package=THT]
  In_12V = male pin header, 2 pins [form="♂ (male)"]
  74HC165 = 74HC595 [package="DIP16 [THT]"]
  entradas_sinal = male pin header, 8 pins [form="♂ (male)"]
  R17 = Resistor [tolerance=±5% resistance=10k package=THT]
  R18 = Resistor [tolerance=±5% resistance=10k package=THT]
  R19 = Resistor [tolerance=±5% resistance=10k package=THT]
  R20 = Resistor [tolerance=±5% resistance=10k package=THT]
  R21 = Resistor [tolerance=±5% resistance=10k package=THT]
  R22 = Resistor [tolerance=±5% resistance=10k package=THT]
  R23 = Resistor [tolerance=±5% resistance=10k package=THT]
  R24 = Resistor [tolerance=±5% resistance=10k package=THT]
  C1 = Electrolytic Capacitor [capacitance=0.1mF package="100 mil [THT, electrolytic]"]
  S1 = Pushbutton [package="[THT]"]
  S2 = Pushbutton [package="[THT]"]
  S3 = Pushbutton [package="[THT]"]
  S4 = Pushbutton [package="[THT]"]
  S5 = Pushbutton [package="[THT]"]
  S6 = Pushbutton [package="[THT]"]
  S7 = Pushbutton [package="[THT]"]
  S8 = Pushbutton [package="[THT]"]
  LED3 = LED - 5mm [color="Red (633nm)" package="5 mm [THT]"]
  Q9 = NPN-Transistor [package="TO92 [THT]"]
  Q10 = NPN-Transistor [package="TO92 [THT]"]
  Q11 = NPN-Transistor [package="TO92 [THT]"]
  Q12 = NPN-Transistor [package="TO92 [THT]"]
  Q13 = NPN-Transistor [package="TO92 [THT]"]
  Q14 = NPN-Transistor [package="TO92 [THT]"]
  Q15 = NPN-Transistor [package="TO92 [THT]"]
  Out_12V = male pin header, 2 pins [form="♂ (male)"]
  D_165 = male pin header, 3 pins [form="♂ (male)"]
  O/7 = female pin header, 2 pins [form="♀ (female)"]
  O/5 = female pin header, 2 pins [form="♀ (female)"]
  O/6 = female pin header, 2 pins [form="♀ (female)"]
  O/4 = female pin header, 2 pins [form="♀ (female)"]
  O/3 = female pin header, 2 pins [form="♀ (female)"]
  O/2 = female pin header, 2 pins [form="♀ (female)"]
  O/1 = female pin header, 2 pins [form="♀ (female)"]
  O/0 = female pin header, 2 pins [form="♀ (female)"]
  out_5V = male pin header, 2 pins [form="♂ (male)"]
  in_5V = male pin header, 2 pins [form="♂ (male)"]
  in_shif = male pin header, 3 pins [form="♂ (male)"]
  out_shift = male pin header, 3 pins [form="♂ (male)"]
  Leds = male pin header, 2 pins [form="♂ (male)"]
  D_165_2 = female pin header, 3 pins [form="♀ (female)"]
  O_165 = female pin header, 3 pins [form="♀ (female)"]

nets:
  N1: 74HC595.Q1, LED2.anode, R10.Pin_1
  N2: 74HC595.Q2, R11.Pin_1, LED3.anode
  N3: 74HC595.Q3, LED4.anode, R12.Pin_1
  N4: 74HC595.Q4, LED5.anode, R13.Pin_1
  N5: 74HC595.Q5, LED6.anode, R14.Pin_1
  N6: 74HC595.Q6, LED7.anode, R15.Pin_1
  N7: 74HC595.Q7, LED8.anode, R16.Pin_1
  GND: 74HC595.GND, 74HC595.OE, In_12V.pin2, 74HC165.GND, R17.Pin_1, R18.Pin_1, R19.Pin_1, R20.Pin_1, R21.Pin_1, R22.Pin_1, R23.Pin_1, R24.Pin_1, C1.-, Out_12V.pin2, O/7.pin2, O/5.pin2, O/6.pin2, O/4.pin2, O/3.pin2, O/2.pin2, O/1.pin2, O/0.pin2, out_5V.pin2, in_5V.pin2, Leds.pin2
  N8: 74HC595.Q7', out_shift.pin1
  5V: 74HC595.MR, 74HC595.VCC, 74HC165.VCC, C1.+, S1.Pin_3, S1.Pin_4, S2.Pin_3, S2.Pin_4, S3.Pin_3, S3.Pin_4, S4.Pin_3, S4.Pin_4, S5.Pin_3, S5.Pin_4, S6.Pin_3, S6.Pin_4, S7.Pin_3, S7.Pin_4, S8.Pin_3, S8.Pin_4, out_5V.pin1, in_5V.pin1
  N9: 74HC595.SH_CP, in_shif.pin3, out_shift.pin3
  N10: 74HC595.ST_CP, in_shif.pin2, out_shift.pin2
  N11: 74HC595.DS, in_shif.pin1
  N12: 74HC595.Q0, LED1.anode, R9.Pin_1
  N13: Q1.E, O/0.pin1
  N14: Q1.B, R9.Pin_0
  12V: Q1.C, In_12V.pin1, Q9.C, Q10.C, Q11.C, Q12.C, Q13.C, Q14.C, Q15.C, Out_12V.pin1
  N15: LED1.cathode, R1.Pin_1
  N16: LED2.cathode, R2.Pin_1
  N17: LED4.cathode, R4.Pin_1
  N18: LED5.cathode, R5.Pin_1
  N19: LED6.cathode, R6.Pin_1
  N20: LED8.cathode, R8.Pin_1
  N21: LED7.cathode, R7.Pin_1
  N22: R1.Pin_0, R2.Pin_0, R3.Pin_0, R4.Pin_0, R5.Pin_0, R6.Pin_0, R7.Pin_0, R8.Pin_0, Leds.pin1
  N23: R3.Pin_1, LED3.cathode
  N24: R10.Pin_0, Q9.B
  N25: R11.Pin_0, Q10.B
  N26: R12.Pin_0, Q11.B
  N27: R13.Pin_0, Q12.B
  N28: R14.Pin_0, Q13.B
  N29: R15.Pin_0, Q14.B
  N30: R16.Pin_0, Q15.B
  N31: 74HC165.Q1, D_165.pin2, D_165_2.pin2
  N32: 74HC165.Q2, D_165.pin3, D_165_2.pin3
  N33: 74HC165.Q3, entradas_sinal.pin5, R21.Pin_0, S5.Pin_1, S5.Pin_2
  N34: 74HC165.Q4, entradas_sinal.pin6, R22.Pin_0, S6.Pin_1, S6.Pin_2
  N35: 74HC165.Q5, entradas_sinal.pin7, R23.Pin_0, S7.Pin_1, S7.Pin_2
  N36: 74HC165.Q6, entradas_sinal.pin8, R24.Pin_0, S8.Pin_1, S8.Pin_2
  N37: 74HC165.Q7, O_165.pin3
  N38: 74HC165.Q7', O_165.pin2
  N39: 74HC165.MR, O_165.pin1
  N40: 74HC165.SH_CP, entradas_sinal.pin1, R17.Pin_0, S1.Pin_1, S1.Pin_2
  N41: 74HC165.ST_CP, entradas_sinal.pin2, R18.Pin_0, S2.Pin_1, S2.Pin_2
  N42: 74HC165.OE, entradas_sinal.pin3, R19.Pin_0, S3.Pin_1, S3.Pin_2
  N43: 74HC165.DS, entradas_sinal.pin4, R20.Pin_0, S4.Pin_1, S4.Pin_2
  N44: 74HC165.Q0, D_165.pin1, D_165_2.pin1
  N45: Q9.E, O/1.pin1
  N46: Q10.E, O/2.pin1
  N47: Q11.E, O/3.pin1
  N48: Q12.E, O/4.pin1
  N49: Q13.E, O/5.pin1
  N50: Q14.E, O/6.pin1
  N51: Q15.E, O/7.pin1
