# Fritzing sketch fonte (saved by Fritzing 0.9.3b)
circuit board: 10cm x 2cm
breadboards: 1

parts:
  Power_plug1 = Power plug
  Power_plug2 = Power plug
  Power_plug3 = Power plug
  Fuse1 = Fuse with Handler [part_number=Htc-15m]
  Fuse2 = Fuse with Handler [part_number=Htc-15m]
  J3 = female pin header, 15 pins [form="♀ (female)"]
  J1 = female pin header, 15 pins [form="♀ (female)"]
  J4 = female pin header, 15 pins [form="♀ (female)"]
  J2 = female pin header, 15 pins [form="♀ (female)"]

nets:
  GND: Power_plug1.GND, Power_plug2.GND, Power_plug3.GND, J1.pin1, J1.pin13, J1.pin14, J1.pin15, J2.pin1, J2.pin15
  N1: Power_plug1.VCC, Fuse1.Connector2, J4.pin1, J4.pin13, J4.pin15
  N2: Power_plug2.VCC, Fuse1.Connector1
  N3: Power_plug3.VCC, Fuse2.Connector1
  N4: Fuse2.Connector2, J3.pin1, J3.pin13, J3.pin14, J3.pin15
