# Fritzing sketch rele_mini (saved by Fritzing 0.9.3b)
circuit board: 25cm x 10cm
breadboards: 1

parts:
  Relé5 = songle relay
  J9 = male pin header, 3 pins [form="♂ (male)"]
  J10 = female pin header, 2 pins [form="♀ (female)"]
  D5 = Rectifier Diode [part_number=1N4001 package="300 mil [THT]"]
  Pad13 = Pad [width=4 height=19.7 connect=center]  # not connected
  Pad14 = Pad [width=4 height=5.6 connect=center]  # not connected
  Pad15 = Pad [width=4 height=5.6 connect=center]  # not connected
  Relé8 = songle relay
  J14 = male pin header, 3 pins [form="♂ (male)"]
  J17 = female pin header, 2 pins [form="♀ (female)"]
  D8 = Rectifier Diode [part_number=1N4001 package="300 mil [THT]"]
  Pad20 = Pad [width=4 height=19.7 connect=center]  # not connected
  Pad24 = Pad [width=4 height=5.6 connect=center]  # not connected
  Pad27 = Pad [width=4 height=5.6 connect=center]  # not connected
  Relé13 = songle relay
  J27 = male pin header, 3 pins [form="♂ (male)"]
  J30 = female pin header, 2 pins [form="♀ (female)"]
  D15 = Rectifier Diode [part_number=1N4001 package="300 mil [THT]"]
  Pad39 = Pad [width=4 height=19.7 connect=center]  # not connected
  Pad42 = Pad [width=4 height=5.6 connect=center]  # not connected
  Pad45 = Pad [width=4 height=5.6 connect=center]  # not connected
  Relé38 = songle relay
  Relé41 = songle relay
  Relé44 = songle relay
  Pad115 = Pad [width=4 height=5.6 connect=center]  # not connected
  Pad116 = Pad [width=4 height=5.6 connect=center]  # not connected
  Pad117 = Pad [width=4 height=5.6 connect=center]  # not connected
  J85 = male pin header, 3 pins [form="♂ (male)"]
  J86 = male pin header, 3 pins [form="♂ (male)"]
  J87 = male pin header, 3 pins [form="♂ (male)"]
  J88 = female pin header, 2 pins [form="♀ (female)"]
  J89 = female pin header, 2 pins [form="♀ (female)"]
  D43 = Rectifier Diode [part_number=1N4001 package="300 mil [THT]"]
  D44 = Rectifier Diode [part_number=1N4001 package="300 mil [THT]"]
  Pad127 = Pad [width=4 height=19.7 connect=center]  # not connected
  Pad128 = Pad [width=4 height=19.7 connect=center]  # not connected
  Pad129 = Pad [width=4 height=5.6 connect=center]  # not connected
  Pad130 = Pad [width=4 height=5.6 connect=center]  # not connected
  Pad131 = Pad [width=4 height=5.6 connect=center]  # not connected
  Pad132 = Pad [width=4 height=5.6 connect=center]  # not connected
  J90 = female pin header, 2 pins [form="♀ (female)"]
  D45 = Rectifier Diode [part_number=1N4001 package="300 mil [THT]"]
  Pad133 = Pad [width=4 height=19.7 connect=center]  # not connected
  Pad134 = Pad [width=4 height=5.6 connect=center]  # not connected
  Pad135 = Pad [width=4 height=5.6 connect=center]  # not connected
  U1 = DSUN-DC Adapter  # not connected
  U2 = ESP8266 WiFi Module [part_number=ESP8266]  # not connected
  U3 = ESP8266-12 WiFi Module [part_number=ESP8266]  # not connected
  HLK-PM1 = HLK-PM01  # not connected
  Componente1 = OMRON PCB Power Relay – G5LE [part_number="G5LE-1\n" package=THT]  # not connected
  J76 = female pin header, 2 pins [form="♀ (female)"]
  J77 = female pin header, 2 pins [form="♀ (female)"]
  J74 = male pin header, 3 pins [form="♂ (male)"]
  Pad114 = Pad [width=4 height=5.6 connect=center]  # not connected
  D39 = Rectifier Diode [part_number=1N4001 package="300 mil [THT]"]
  D37 = Rectifier Diode [part_number=1N4001 package="300 mil [THT]"]
  D38 = Rectifier Diode [part_number=1N4001 package="300 mil [THT]"]
  Relé36 = songle relay
  Relé40 = songle relay
  Pad113 = Pad [width=4 height=5.6 connect=center]  # not connected
  J75 = male pin header, 3 pins [form="♂ (male)"]
  J78 = female pin header, 2 pins [form="♀ (female)"]
  J73 = male pin header, 3 pins [form="♂ (male)"]
  Pad111 = Pad [width=4 height=19.7 connect=center]  # not connected
  Pad112 = Pad [width=4 height=5.6 connect=center]  # not connected
  Pad110 = Pad [width=4 height=19.7 connect=center]  # not connected
  Pad109 = Pad [width=4 height=19.7 connect=center]  # not connected
  Relé43 = songle relay
  Relé45 = songle relay  # not connected
  J106 = female pin header, 1 pin [form="♀ (female)"]  # not connected
  J107 = female pin header, 1 pin [form="♀ (female)"]  # not connected
  J108 = female pin header, 1 pin [form="♀ (female)"]  # not connected
  J109 = female pin header, 1 pin [form="♀ (female)"]  # not connected
  J110 = female pin header, 1 pin [form="♀ (female)"]  # not connected

nets:
  N1: Relé5.VCC, J10.pin1, D5.cathode
  N2: Relé5.NO, J9.pin3
  N3: Relé5.NC, J9.pin1
  N4: Relé5.COMMON, J9.pin2
  N5: Relé5.GND, J10.pin2, D5.anode
  N6: Relé8.VCC, J17.pin1, D8.cathode
  N7: Relé8.NO, J14.pin3
  N8: Relé8.NC, J14.pin1
  N9: Relé8.COMMON, J14.pin2
  N10: Relé8.GND, J17.pin2, D8.anode
  N11: Relé13.VCC, J30.pin1, D15.cathode
  N12: Relé13.NO, J27.pin3
  N13: Relé13.NC, J27.pin1
  N14: Relé13.COMMON, J27.pin2
  N15: Relé13.GND, J30.pin2, D15.anode
  N16: Relé38.VCC, J88.pin1, D43.cathode
  N17: Relé38.NO, J85.pin3
  N18: Relé38.NC, J85.pin1
  N19: Relé38.COMMON, J85.pin2
  N20: Relé38.GND, J88.pin2, D43.anode
  N21: Relé41.VCC, J89.pin1, D44.cathode
  N22: Relé41.NO, J86.pin3
  N23: Relé41.NC, J86.pin1
  N24: Relé41.COMMON, J86.pin2
  N25: Relé41.GND, J89.pin2, D44.anode
  N26: Relé44.VCC, J90.pin1, D45.cathode
  N27: Relé44.NO, J87.pin3
  N28: Relé44.NC, J87.pin1
  N29: Relé44.COMMON, J87.pin2
  N30: Relé44.GND, J90.pin2, D45.anode
  N31: J76.pin1, D37.cathode, Relé36.VCC
  N32: J76.pin2, D37.anode, Relé36.GND
  N33: J77.pin1, D38.cathode, Relé40.VCC
  N34: J77.pin2, D38.anode, Relé40.GND
  N35: J74.pin1, Relé40.NC
  N36: J74.pin2, Relé40.COMMON
  N37: J74.pin3, Relé40.NO
  N38: D39.cathode, J78.pin1, Relé43.VCC
  N39: D39.anode, J78.pin2, Relé43.GND
  N40: Relé36.NO, J73.pin3
  N41: Relé36.NC, J73.pin1
  N42: Relé36.COMMON, J73.pin2
  N43: J75.pin1, Relé43.NC
  N44: J75.pin2, Relé43.COMMON
  N45: J75.pin3, Relé43.NO

notes:
  +
  -

custom parts:
  DSUN-DC Adapter: DSUN-DC Adapter with variable input/output
  ESP8266 WiFi Module: Generic WiFi Module based on the ESP8266 with onboard PCB antenna and UART communications
  ESP8266-12 WiFi Module: Generic WiFi Module based on the ESP8266 with onboard PCB antenna and UART communications
  HLK-PM01: AC-DC 220V to 5V Step-Down Power Supply Module
