# Fritzing sketch wifi (saved by Fritzing 0.9.3b)
circuit board: 5.3cm x 2cm
breadboards: 1

parts:
  J2 = double row rounded female pin header, 8 pins [form="♀ (female rounded)"]
  S1 = Pushbutton [package="[THT]"]
  R1 = Resistor [tolerance=±5% resistance=220 package=THT]
  R2 = Resistor [tolerance=±5% resistance=220 package=THT]
  R3 = Resistor [tolerance=±5% resistance=220 package=THT]
  R4 = Resistor [tolerance=±5% resistance=220 package=THT]
  J3 = female pin header, 2 pins [form="♀ (female)"]
  J1 = female pin header, 4 pins [form="♀ (female)"]
  J4 = female pin header, 2 pins [form="♀ (female)"]
  LED1 = LED - 5mm [color="Red (633nm)" package="5 mm [THT]"]

nets:
  N1: J2.pin1, J1.pin1
  N2: J2.pin2, R2.Pin_0
  N3: J2.pin4, R2.Pin_1, R4.Pin_1, J1.pin3
  N4: J2.pin5, R1.Pin_0, R3.Pin_0
  N5: J2.pin6, J3.pin1
  N6: J2.pin8, S1.Pin_1, S1.Pin_2, R3.Pin_1, J1.pin4, J4.pin2
  N7: S1.Pin_3, S1.Pin_4, J3.pin2
  N8: R1.Pin_1, J1.pin2
  N9: R4.Pin_0, LED1.cathode
  N10: J4.pin1, LED1.anode
